// Digital circuit Adder32.dig as structural Verilog
module Adder32 (
  input  Cin,
  input  [31:0] A,
  input  [31:0] B,
  output [31:0] A_plus_B,
  output Cout
);

  wire [31:0] and_1_out, and_2_out, xor_1_out;
  wire [31:1] or_1_out;

  assign xor_1_out = A ^ B;  // XOr xor_1, 32 bits wide
  assign and_1_out = A & B;  // And and_1, 32 bits wide
  assign and_2_out = {or_1_out, Cin} & xor_1_out;  // And and_2, 32 bits wide
  assign A_plus_B = {or_1_out, Cin} ^ xor_1_out;  // XOr xor_2, 32 bits wide
  assign {Cout, or_1_out} = and_1_out | and_2_out;  // Or or_1, 32 bits wide
endmodule
