// Digital circuit Interface test.dig as structural Verilog
module Interface_test (
  input  in_2,
  input  [31:0] in_3,
  input  in_4,
  output [31:0] out_1,
  output [31:0] out_5,
  output out_6,
  output out_7,
  output [31:0] out_8,
  output [31:0] out_9
);

  wire addr, clock, d_ff_1_q, d_ff_2_q, d_ff_3_q, d_ff_5_q, d_ff_6_q, d_ff_7_q, d_ff_8_q,
       demultiplexer_1_out_0, demultiplexer_1_out_1, finished, interface_1_p6, ldREG, not_1_out, or_1_out,
       read_t, STEPS, write_t;
  wire [11:1] interface_1_p7;

  not not_1 (not_1_out, STEPS);
  PullDown pulldown_1 (.out(STEPS));
  PullDown pulldown_2 (.out(write_t));
  PullDown pulldown_3 (.out(read_t));
  PullDown pulldown_4 (.out(addr));
  PullDown pulldown_5 (.out(ldREG));
  D_FF d_ff_1 (.D(not_1_out), .C(clock), .Q(d_ff_1_q));  // open: nQ
  assign out_5 = d_ff_1_q ? 32'ha0 : 32'bz;  // Driver driver_1
  assign write_t = d_ff_1_q ? 1'b0 : 1'bz;  // Driver driver_2
  assign read_t = d_ff_1_q ? 1'b0 : 1'bz;  // Driver driver_3
  assign addr = d_ff_1_q ? 1'b1 : 1'bz;  // Driver driver_4
  assign STEPS = d_ff_1_q ? 1'b1 : 1'bz;  // Driver driver_5
  or or_1 (or_1_out, d_ff_1_q, demultiplexer_1_out_0);
  D_FF d_ff_2 (.D(or_1_out), .C(clock), .Q(d_ff_2_q));  // open: nQ
  assign write_t = d_ff_2_q ? 1'b0 : 1'bz;  // Driver driver_6
  assign read_t = d_ff_2_q ? 1'b1 : 1'bz;  // Driver driver_7
  assign addr = d_ff_2_q ? 1'b0 : 1'bz;  // Driver driver_8
  assign STEPS = d_ff_2_q ? 1'b1 : 1'bz;  // Driver driver_9
  Demultiplexer demultiplexer_1 (
    .sel(finished), .in(d_ff_2_q), .out_0(demultiplexer_1_out_0), .out_1(demultiplexer_1_out_1));
  // Interface interface_1: pin names not known; wires that end beside it: out_5, out_9, in_4, {{9{1'b0}}, addr, read_t, write_t}, clock, interface_1_p6, {interface_1_p7, finished}, out_5, out_9, out_8, out_7, out_6
  D_FF d_ff_3 (.D(demultiplexer_1_out_1), .C(clock), .Q(d_ff_3_q));  // open: nQ
  assign ldREG = d_ff_3_q ? 1'b1 : 1'bz;  // Driver driver_10
  assign write_t = d_ff_3_q ? 1'b0 : 1'bz;  // Driver driver_11
  assign read_t = d_ff_3_q ? 1'b0 : 1'bz;  // Driver driver_12
  assign addr = d_ff_3_q ? 1'b0 : 1'bz;  // Driver driver_13
  D_FF d_ff_4 (.D(d_ff_3_q), .C(clock), .Q(interface_1_p6));  // open: nQ
  assign STEPS = d_ff_3_q ? 1'b1 : 1'bz;  // Driver driver_14
  assign STEPS = interface_1_p6 ? 1'b1 : 1'bz;  // Driver driver_15
  assign write_t = interface_1_p6 ? 1'b0 : 1'bz;  // Driver driver_16
  assign read_t = interface_1_p6 ? 1'b0 : 1'bz;  // Driver driver_17
  assign addr = interface_1_p6 ? 1'b0 : 1'bz;  // Driver driver_18
  D_FF d_ff_5 (.D(interface_1_p6), .C(clock), .Q(d_ff_5_q));  // open: nQ
  assign write_t = d_ff_5_q ? 1'b0 : 1'bz;  // Driver driver_19
  assign read_t = d_ff_5_q ? 1'b0 : 1'bz;  // Driver driver_20
  assign addr = d_ff_5_q ? 1'b0 : 1'bz;  // Driver driver_21
  assign STEPS = d_ff_5_q ? 1'b1 : 1'bz;  // Driver driver_22
  Button button_1 (.out(clock));
  Register #(.Bits(32)) register_1 (.D(out_5), .C(~clock), .en(ldREG), .Q(out_1));
  D_FF d_ff_6 (.D(d_ff_5_q), .C(clock), .Q(d_ff_6_q));  // open: nQ
  assign write_t = d_ff_6_q ? 1'b0 : 1'bz;  // Driver driver_23
  assign read_t = d_ff_6_q ? 1'b0 : 1'bz;  // Driver driver_24
  assign addr = d_ff_6_q ? 1'b0 : 1'bz;  // Driver driver_25
  assign STEPS = d_ff_6_q ? 1'b1 : 1'bz;  // Driver driver_26
  D_FF d_ff_7 (.D(d_ff_6_q), .C(clock), .Q(d_ff_7_q));  // open: nQ
  assign write_t = d_ff_7_q ? 1'b0 : 1'bz;  // Driver driver_27
  assign read_t = d_ff_7_q ? 1'b0 : 1'bz;  // Driver driver_28
  assign addr = d_ff_7_q ? 1'b0 : 1'bz;  // Driver driver_29
  D_FF d_ff_8 (.D(d_ff_7_q), .C(clock), .Q(d_ff_8_q));  // open: nQ
  assign STEPS = d_ff_7_q ? 1'b1 : 1'bz;  // Driver driver_30
  assign STEPS = d_ff_8_q ? 1'b1 : 1'bz;  // Driver driver_31
  assign write_t = d_ff_8_q ? 1'b0 : 1'bz;  // Driver driver_32
  assign read_t = d_ff_8_q ? 1'b0 : 1'bz;  // Driver driver_33
  assign addr = d_ff_8_q ? 1'b0 : 1'bz;  // Driver driver_34
  assign out_9 = in_2 ? in_3 : 32'bz;  // Driver driver_35

  // Other names for the same wires on the sheet: ABUS[31:0] = out_8; DBUS[31:0] = out_9; FC = in_4;
  //   IBUS[31:0] = out_5; READ = out_6; WRITE = out_7

  // Notes on the sheet:
  //   in_3: default 255
endmodule
