// Digital circuit Interface.dig as structural Verilog
module Interface (
  input  [31:0] IBUS_in,
  input  [31:0] DBUS_in,
  input  FC,
  input  [11:0] control_in,
  input  clock,
  output [11:0] control_out,
  output [31:0] IBUS_out,
  output [31:0] DBUS_out,
  output [31:0] ABUS,
  output WRITE,
  output READ
);

  wire and_3_out, and_4_out, d_ff_1_nq, d_ff_2_nq, d_ff_3_q, d_ff_4_nq, d_ff_5_nq, d_ff_7_nq, d_ff_8_q,
       d_ff_9_q, FC_re, mdr_out_ibus, or_1_out, or_2_out, or_3_out, read_re, readFF, readFF_re, write_re,
       writeFF, writeFF_re;
  wire [31:0] MAR_q, MDR_q, multiplexer_1_out;

  D_FF d_ff_1 (.D(control_in[1]), .C(clock), .nQ(d_ff_1_nq));  // open: Q
  D_FF d_ff_2 (.D(control_in[0]), .C(clock), .nQ(d_ff_2_nq));  // open: Q
  and and_1 (read_re, control_in[1], d_ff_1_nq);
  and and_2 (write_re, control_in[0], d_ff_2_nq);
  and and_3 (and_3_out, FC, readFF);
  and and_4 (and_4_out, FC, writeFF);
  RS_FF_AS rs_ff_as_1 (.S(read_re), .R(FC_re), .Q(readFF));  // open: nQ
  RS_FF_AS rs_ff_as_2 (.S(write_re), .R(FC_re), .Q(writeFF));  // open: nQ
  or or_1 (or_1_out, and_3_out, and_4_out);
  Multiplexer #(.Bits(32)) multiplexer_1 (.sel(writeFF_re), .in_0(DBUS_in), .in_1(IBUS_in), .out(multiplexer_1_out));
  or or_2 (or_2_out, writeFF_re, mdr_out_ibus);
  Register #(.Bits(32)) MDR (.D(multiplexer_1_out), .C(~clock), .en(or_2_out), .Q(MDR_q));
  Register #(.Bits(32)) MAR (.D(IBUS_in), .C(~clock), .en(control_in[2]), .Q(MAR_q));
  D_FF d_ff_3 (.D(or_1_out), .C(clock), .Q(d_ff_3_q));  // open: nQ
  D_FF d_ff_4 (.D(readFF), .C(clock), .nQ(d_ff_4_nq));  // open: Q
  D_FF d_ff_5 (.D(writeFF), .C(clock), .nQ(d_ff_5_nq));  // open: Q
  or or_3 (or_3_out, writeFF, readFF);
  D_FF d_ff_6 (.D(mdr_out_ibus), .C(clock), .Q(control_out[0]));  // open: nQ
  and and_5 (readFF_re, readFF, d_ff_4_nq);
  and and_6 (writeFF_re, writeFF, d_ff_5_nq);
  D_FF d_ff_7 (.D(d_ff_3_q), .C(clock), .nQ(d_ff_7_nq));  // open: Q
  assign DBUS_out = writeFF ? MDR_q : 32'bz;  // Driver driver_1
  assign IBUS_out = control_out[0] ? MDR_q : 32'bz;  // Driver driver_2
  assign ABUS = or_3_out ? MAR_q : 32'bz;  // Driver driver_3
  and and_7 (FC_re, d_ff_3_q, d_ff_7_nq);
  D_FF d_ff_8 (.D(readFF), .C(clock), .Q(d_ff_8_q));  // open: nQ
  D_FF d_ff_9 (.D(readFF), .C(clock), .Q(d_ff_9_q));  // open: nQ
  and and_8 (mdr_out_ibus, ~readFF, d_ff_8_q);  // And
  and and_9 (mdr_out_ibus, ~readFF, d_ff_9_q);  // And
  JK_FF_AS jk_ff_as_1 (.Set(1'b0), .J(readFF_re), .C(clock), .K(1'b0), .Clr(~readFF), .Q(READ));  // open: nQ
  JK_FF_AS jk_ff_as_2 (.Set(1'b0), .J(writeFF_re), .C(clock), .K(1'b0), .Clr(~writeFF), .Q(WRITE));  // open: nQ

  assign control_out[11:1] = {11{1'b0}};

  // Other names for the same wires on the sheet: write_t = control_in[0]; read_t = control_in[1];
  //   addr_in = control_in[2]; outputReadValue = control_out[0]; readFF_fe = mdr_out_ibus

  // Notes on the sheet:
  //   IBUS_out: Internal CPU bus
  //   IBUS_in: Internal CPU bus
  //   DBUS_in: Internal CPU bus, default 255
  //   FC: Internal CPU bus
  //   control_in: default 2
  //   clock: Internal CPU bus
  //   Ovo su signali read i write koji se iskljuce cim 
  //   periferija javi da je zavrsila posao, da ne bi bili 
  //   ukljuceni bezveze i nakon toga
  //   Ovo sluzi da filitrira FC, tako da se uzima njegova vrednost samo ukoliko je write ili read ukljucen
  //   Delay outputing the read value by one clock cycle
  //   Kada se FC signal podigne sa 0 na 1 to
  //   znaci da je periferija (ili memorija) 
  //   primila signal (write/read) uradila sta treba pa 
  //   javlja procesoru da je zavrsila
endmodule
