// Digital circuit OperacionaJedinica.dig as structural Verilog
module OperacionaJedinica (
  input  [31:0] in_1,
  input  in_3,
  input  in_4,
  input  [3:0] in_5,
  input  [4:0] in_6,
  input  [4:0] in_7,
  input  [4:0] in_8,
  input  in_9,
  input  in_10,
  input  in_11,
  input  in_12,
  input  in_13,
  input  [1:0] in_14,
  input  in_15,
  output [31:0] BUS,
  output [31:0] IR
);

  wire [31:0] alu_1_out, demultiplexer_1_out_0, demultiplexer_1_out_1, multiplexer_1_out, multiplexer_2_out,
       PC_q, regfile_1_rs1out, regfile_1_rs2out;

  RegFile regfile_1 (
    .DIN(demultiplexer_1_out_0), .SRC1(in_6), .SRC2(in_7), .DEST(in_8), .wrR(in_9), .CLOCK(in_11),
    .RS1OUT(regfile_1_rs1out), .RS2OUT(regfile_1_rs2out));
  Register #(.Bits(32)) PC (.D(alu_1_out), .C(in_11), .en(in_4), .Q(PC_q));
  Register #(.Bits(32)) u_IR (.D(BUS), .C(in_11), .en(in_10), .Q(IR));
  Multiplexer #(.Bits(32)) multiplexer_1 (.sel(in_13), .in_0(PC_q), .in_1(regfile_1_rs1out), .out(multiplexer_1_out));
  Multiplexer #(.Bits(32), .Selector_Bits(2)) multiplexer_2 (
    .sel(in_14), .in_0(regfile_1_rs2out), .in_1({32{1'b0}}), .in_2(32'h4), .in_3(IR), .out(multiplexer_2_out));
  ALU alu_1 (.Op(in_5), .A(multiplexer_1_out), .B(multiplexer_2_out), .Out(alu_1_out));  // open: EQUAL, LESS, LESS_U
  Demultiplexer #(.Bits(32)) demultiplexer_1 (
    .sel(in_15), .in(alu_1_out), .out_0(demultiplexer_1_out_0), .out_1(demultiplexer_1_out_1));
  assign BUS = in_12 ? demultiplexer_1_out_1 : 32'bz;  // Driver driver_1
  assign BUS = in_3 ? in_1 : 32'bz;  // Driver driver_2

  // Other names for the same wires on the sheet: busALU = in_12; clock = in_11; dmuxALU = in_15; ldIR = in_10;
  //   ldPC = in_4; muxAALU = in_13; muxBALU[1:0] = in_14; opALU[3:0] = in_5; rd[4:0] = in_8; rs1[4:0] = in_6;
  //   rs2[4:0] = in_7; wrR = in_9
endmodule
