// Digital circuit mrzime.dig as structural Verilog
module mrzime (
  input  wrR,
  input  [4:0] DEST,
  input  [31:0] DIN,
  input  CLOCK,
  input  [4:0] SRC2,
  input  [4:0] SRC1,
  output [31:0] RS1OUT,
  output [31:0] RS2OUT
);

  wire and_1_out, and_2_out, and_3_out, and_4_out, and_5_out, and_6_out, and_7_out, and_8_out, and_9_out,
       and_10_out, and_11_out, and_12_out, and_13_out, and_14_out, and_15_out, and_16_out, and_17_out,
       and_18_out, and_19_out, and_20_out, and_21_out, and_22_out, and_23_out, and_24_out, and_25_out,
       and_26_out, and_27_out, and_28_out, and_29_out, and_30_out, and_31_out, and_32_out, ldR0, ldR1, ldR2,
       ldR3, ldR4, ldR5, ldR6, ldR7, ldR8, ldR9, ldR10, ldR11, ldR12, ldR13, ldR14, ldR15, ldR16, ldR17,
       ldR18, ldR19, ldR20, ldR21, ldR22, ldR23, ldR24, ldR25, ldR26, ldR27, ldR28, ldR29, ldR30, ldR31;
  wire [31:0] ldR31__0, R0OUT, R1OUT, R2OUT, R3OUT, R4OUT, R5OUT, R6OUT, R7OUT, R8OUT, R9OUT, R10OUT, R11OUT,
       R12OUT, R13OUT, R14OUT, R15OUT, R16OUT, R17OUT, R18OUT, R19OUT, R20OUT, R21OUT, R22OUT, R23OUT,
       R24OUT, R25OUT, R26OUT, R27OUT, R28OUT, R29OUT, R30OUT, R31OUT;

  Decoder #(.Selector_Bits(5)) decoder_1 (
    .sel(DEST), .out_0(ldR31__0[0]), .out_1(ldR31__0[1]), .out_2(ldR31__0[2]), .out_3(ldR31__0[3]),
    .out_4(ldR31__0[4]), .out_5(ldR31__0[5]), .out_6(ldR31__0[6]), .out_7(ldR31__0[7]), .out_8(ldR31__0[8]),
    .out_9(ldR31__0[9]), .out_10(ldR31__0[10]), .out_11(ldR31__0[11]), .out_12(ldR31__0[12]),
    .out_13(ldR31__0[13]), .out_14(ldR31__0[14]), .out_15(ldR31__0[15]), .out_16(ldR31__0[16]),
    .out_17(ldR31__0[17]), .out_18(ldR31__0[18]), .out_19(ldR31__0[19]), .out_20(ldR31__0[20]),
    .out_21(ldR31__0[21]), .out_22(ldR31__0[22]), .out_23(ldR31__0[23]), .out_24(ldR31__0[24]),
    .out_25(ldR31__0[25]), .out_26(ldR31__0[26]), .out_27(ldR31__0[27]), .out_28(ldR31__0[28]),
    .out_29(ldR31__0[29]), .out_30(ldR31__0[30]), .out_31(ldR31__0[31]));
  and and_1 (and_1_out, wrR, ldR0);
  and and_2 (and_2_out, wrR, ldR1);
  and and_3 (and_3_out, wrR, ldR2);
  and and_4 (and_4_out, wrR, ldR3);
  and and_5 (and_5_out, wrR, ldR4);
  and and_6 (and_6_out, wrR, ldR5);
  and and_7 (and_7_out, wrR, ldR6);
  and and_8 (and_8_out, wrR, ldR7);
  Register #(.Bits(32)) register_1 (.D(DIN), .C(CLOCK), .en(and_1_out), .Q(R0OUT));
  Register #(.Bits(32)) register_2 (.D(DIN), .C(CLOCK), .en(and_2_out), .Q(R1OUT));
  Register #(.Bits(32)) register_3 (.D(DIN), .C(CLOCK), .en(and_3_out), .Q(R2OUT));
  Register #(.Bits(32)) register_4 (.D(DIN), .C(CLOCK), .en(and_4_out), .Q(R3OUT));
  Register #(.Bits(32)) register_5 (.D(DIN), .C(CLOCK), .en(and_5_out), .Q(R4OUT));
  Register #(.Bits(32)) register_6 (.D(DIN), .C(CLOCK), .en(and_6_out), .Q(R5OUT));
  Register #(.Bits(32)) register_7 (.D(DIN), .C(CLOCK), .en(and_7_out), .Q(R6OUT));
  Register #(.Bits(32)) register_8 (.D(DIN), .C(CLOCK), .en(and_8_out), .Q(R7OUT));
  and and_9 (and_9_out, wrR, ldR8);
  and and_10 (and_10_out, wrR, ldR9);
  and and_11 (and_11_out, wrR, ldR10);
  and and_12 (and_12_out, wrR, ldR11);
  and and_13 (and_13_out, wrR, ldR12);
  and and_14 (and_14_out, wrR, ldR13);
  and and_15 (and_15_out, wrR, ldR14);
  and and_16 (and_16_out, wrR, ldR15);
  Register #(.Bits(32)) register_9 (.D(DIN), .C(CLOCK), .en(and_9_out), .Q(R8OUT));
  Register #(.Bits(32)) register_10 (.D(DIN), .C(CLOCK), .en(and_10_out), .Q(R9OUT));
  Register #(.Bits(32)) register_11 (.D(DIN), .C(CLOCK), .en(and_11_out), .Q(R10OUT));
  Register #(.Bits(32)) register_12 (.D(DIN), .C(CLOCK), .en(and_12_out), .Q(R11OUT));
  Register #(.Bits(32)) register_13 (.D(DIN), .C(CLOCK), .en(and_13_out), .Q(R12OUT));
  Register #(.Bits(32)) register_14 (.D(DIN), .C(CLOCK), .en(and_14_out), .Q(R13OUT));
  Register #(.Bits(32)) register_15 (.D(DIN), .C(CLOCK), .en(and_15_out), .Q(R14OUT));
  Register #(.Bits(32)) register_16 (.D(DIN), .C(CLOCK), .en(and_16_out), .Q(R15OUT));
  and and_17 (and_17_out, wrR, ldR16);
  and and_18 (and_18_out, wrR, ldR17);
  and and_19 (and_19_out, wrR, ldR18);
  and and_20 (and_20_out, wrR, ldR19);
  and and_21 (and_21_out, wrR, ldR20);
  and and_22 (and_22_out, wrR, ldR21);
  and and_23 (and_23_out, wrR, ldR22);
  and and_24 (and_24_out, wrR, ldR23);
  Register #(.Bits(32)) register_17 (.D(DIN), .C(CLOCK), .en(and_17_out), .Q(R16OUT));
  Register #(.Bits(32)) register_18 (.D(DIN), .C(CLOCK), .en(and_18_out), .Q(R17OUT));
  Register #(.Bits(32)) register_19 (.D(DIN), .C(CLOCK), .en(and_19_out), .Q(R18OUT));
  Register #(.Bits(32)) register_20 (.D(DIN), .C(CLOCK), .en(and_20_out), .Q(R19OUT));
  Register #(.Bits(32)) register_21 (.D(DIN), .C(CLOCK), .en(and_21_out), .Q(R20OUT));
  Register #(.Bits(32)) register_22 (.D(DIN), .C(CLOCK), .en(and_22_out), .Q(R21OUT));
  Register #(.Bits(32)) register_23 (.D(DIN), .C(CLOCK), .en(and_23_out), .Q(R22OUT));
  Register #(.Bits(32)) register_24 (.D(DIN), .C(CLOCK), .en(and_24_out), .Q(R23OUT));
  and and_25 (and_25_out, wrR, ldR24);
  and and_26 (and_26_out, wrR, ldR25);
  and and_27 (and_27_out, wrR, ldR26);
  and and_28 (and_28_out, wrR, ldR27);
  and and_29 (and_29_out, wrR, ldR28);
  and and_30 (and_30_out, wrR, ldR29);
  and and_31 (and_31_out, wrR, ldR30);
  and and_32 (and_32_out, wrR, ldR31);
  Register #(.Bits(32)) register_25 (.D(DIN), .C(CLOCK), .en(and_25_out), .Q(R24OUT));
  Register #(.Bits(32)) register_26 (.D(DIN), .C(CLOCK), .en(and_26_out), .Q(R25OUT));
  Register #(.Bits(32)) register_27 (.D(DIN), .C(CLOCK), .en(and_27_out), .Q(R26OUT));
  Register #(.Bits(32)) register_28 (.D(DIN), .C(CLOCK), .en(and_28_out), .Q(R27OUT));
  Register #(.Bits(32)) register_29 (.D(DIN), .C(CLOCK), .en(and_29_out), .Q(R28OUT));
  Register #(.Bits(32)) register_30 (.D(DIN), .C(CLOCK), .en(and_30_out), .Q(R29OUT));
  Register #(.Bits(32)) register_31 (.D(DIN), .C(CLOCK), .en(and_31_out), .Q(R30OUT));
  Register #(.Bits(32)) register_32 (.D(DIN), .C(CLOCK), .en(and_32_out), .Q(R31OUT));
  Multiplexer #(.Bits(32), .Selector_Bits(5)) multiplexer_1 (
    .sel(SRC1), .in_0(R0OUT), .in_1(R1OUT), .in_2(R2OUT), .in_3(R3OUT), .in_4(R4OUT), .in_5(R5OUT),
    .in_6(R6OUT), .in_7(R7OUT), .in_8(R8OUT), .in_9(R9OUT), .in_10(R10OUT), .in_11(R11OUT), .in_12(R12OUT),
    .in_13(R13OUT), .in_14(R14OUT), .in_15(R15OUT), .in_16(R16OUT), .in_17(R17OUT), .in_18(R18OUT),
    .in_19(R19OUT), .in_20(R20OUT), .in_21(R21OUT), .in_22(R22OUT), .in_23(R23OUT), .in_24(R24OUT),
    .in_25(R25OUT), .in_26(R26OUT), .in_27(R27OUT), .in_28(R28OUT), .in_29(R29OUT), .in_30(R30OUT),
    .in_31(R31OUT), .out(RS1OUT));
  Multiplexer #(.Selector_Bits(5), .Bits(32)) multiplexer_2 (
    .sel(SRC2), .in_0(R0OUT), .in_1(R1OUT), .in_2(R2OUT), .in_3(R3OUT), .in_4(R4OUT), .in_5(R5OUT),
    .in_6(R6OUT), .in_7(R7OUT), .in_8(R8OUT), .in_9(R9OUT), .in_10(R10OUT), .in_11(R11OUT), .in_12(R12OUT),
    .in_13(R13OUT), .in_14(R14OUT), .in_15(R15OUT), .in_16(R16OUT), .in_17(R17OUT), .in_18(R18OUT),
    .in_19(R19OUT), .in_20(R20OUT), .in_21(R21OUT), .in_22(R22OUT), .in_23(R23OUT), .in_24(R24OUT),
    .in_25(R25OUT), .in_26(R26OUT), .in_27(R27OUT), .in_28(R28OUT), .in_29(R29OUT), .in_30(R30OUT),
    .in_31(R31OUT), .out(RS2OUT));

  // Other names for the same wires on the sheet: clk = CLOCK; D31__0[31:0] = DIN; wr = wrR
endmodule
